# Fritzing sketch A5 (saved by Fritzing 0.9.3b)
breadboards: 1

parts:
  J1 = Basic Servo
  Part1 = Thumb Joystick
  Part2 = Arduino Uno (Rev3)

nets:
  GND: J1.gnd, Part1.GND, Part2.GND
  VCC: J1.vcc, Part1.VCC, Part2.5V
  N1: J1.pulse, Part2.D9_PWM
  N2: Part1.HORZ, Part2.A0
  N3: Part1.VERT, Part2.A1
